# Fritzing sketch sketch (saved by Fritzing 0.9.3b)

parts:
  Raspberry_Pi_1 = Raspberry Pi 3 [part_number=RPI-3-V1.2]
  S1 = Round Pushbutton
  NEOPIXEL1 = Neopixel Strip -- Black (30/m)
  NEOPIXEL2 = Neopixel Strip -- Black (30/m)
  Bauteil3 = Thermal Printer
  JACK1 = 2.1mm Barrel Jack with Terminal Block

nets:
  GND: Raspberry_Pi_1.GND, S1.leg0, NEOPIXEL1.GND, NEOPIXEL2.GND, Bauteil3.GND#2
  N1: Raspberry_Pi_1.GIPO23, S1.leg1
  N2: Raspberry_Pi_1.GIPO18, NEOPIXEL1.Din, NEOPIXEL2.Din
  N3: Raspberry_Pi_1.GIPO15, Bauteil3.TXD
  N4: Raspberry_Pi_1.GIPO14, Bauteil3.RXD
  +5V: Raspberry_Pi_1.5V, NEOPIXEL1.+5V, NEOPIXEL2.+5V
  N5: Bauteil3.GND#0, JACK1.NEG
  N6: Bauteil3.VH, JACK1.POS

custom parts:
  Neopixel Strip -- Black (30/m): These NeoPixel strips have 30 digitally-addressable pixel LEDs per meter and are very affordable and are only 12.5 mm wide, 10 mm if you remove the strip from the casing.
